// Logisim project cpu.circ as structural Verilog: 1 circuit, main circuit main
module main (
  input  [3:0] in_1,
  input  in_2
);

  wire clock_2_out, clock_3_out, decoder_1_out0, decoder_1_out1, decoder_1_out2, decoder_1_out3,
       decoder_1_out4, decoder_1_out5, decoder_1_out6, decoder_1_out7, decoder_1_out8, decoder_1_out9,
       decoder_1_out10, decoder_1_out11, decoder_1_out12, LOAD_IMM, MEM_READ, MEM_TO_REG, MEM_WRITE, MUX_IMM,
       or_1_out, PC_ADRESS, pc_main_1_p3, undriven;
  wire [3:0] ALU_OP, or_8_out;
  wire [15:0] alu_main_1_s, bit_extender_1_out, bit_extender_2_out, multiplexer_1_out, multiplexer_3_out,
       pc_main_1_p1, pc_main_1_p4, ram_1_dout, reg_file_1_a, reg_file_1_b, rom_1_data;

  // PC_Main pc_main_1: pin names not known; wires that end beside it: pc_main_1_p1, PC_ADRESS, pc_main_1_p3, pc_main_1_p4
  Clock clock_1 (.out(pc_main_1_p3));
  Decoder #(.select(4)) decoder_1 (
    .out0(decoder_1_out0), .out1(decoder_1_out1), .out2(decoder_1_out2), .out3(decoder_1_out3),
    .out4(decoder_1_out4), .out5(decoder_1_out5), .out6(decoder_1_out6), .out7(decoder_1_out7),
    .out8(decoder_1_out8), .out9(decoder_1_out9), .out10(decoder_1_out10), .out11(decoder_1_out11),
    .out12(decoder_1_out12), .sel(in_1), .en(in_2));  // open: out13, out14, out15
  ROM #(.addrWidth(16), .dataWidth(16)) rom_1 (.addr(pc_main_1_p4), .data(rom_1_data));
  or or_1 (or_1_out, decoder_1_out0, decoder_1_out1, decoder_1_out2, decoder_1_out3, decoder_1_out4, decoder_1_out5, decoder_1_out6, decoder_1_out7, decoder_1_out8, decoder_1_out9, decoder_1_out10, decoder_1_out11);
  buf or_2 (MEM_READ, decoder_1_out11);  // OR_Gate
  buf or_3 (MEM_WRITE, decoder_1_out12);  // OR_Gate
  // OR_Gate or_4 has open pins: out=PC_ADRESS
  // OR_Gate or_5 has open pins: out=MUX_IMM
  or or_6 (LOAD_IMM, decoder_1_out9, decoder_1_out11, decoder_1_out12);
  buf or_7 (MEM_TO_REG, decoder_1_out11);  // OR_Gate
  or or_8 (or_8_out[0], decoder_1_out1, decoder_1_out3, decoder_1_out5, decoder_1_out7);
  or or_9 (or_8_out[1], decoder_1_out2, decoder_1_out3, decoder_1_out6, decoder_1_out7, decoder_1_out10);
  or or_10 (or_8_out[2], decoder_1_out4, decoder_1_out5, decoder_1_out6, decoder_1_out7);
  buf or_11 (or_8_out[3], decoder_1_out8);  // OR_Gate
  Clock clock_2 (.out(clock_2_out));
  assign bit_extender_1_out = {{12{rom_1_data[11]}}, rom_1_data[11:8]};  // Bit_Extender bit_extender_1
  assign bit_extender_2_out = {{4{rom_1_data[11]}}, rom_1_data[11:0]};  // Bit_Extender bit_extender_2
  REG_File reg_file_1 (
    .Reset(undriven), .Reg_Sel_A(rom_1_data[7:4]), .Reg_Sel_B(rom_1_data[3:0]), .Write_Enable(or_1_out),
    .Write_Reg(rom_1_data[11:8]), .Write_Data(pc_main_1_p1), .CLK(clock_2_out), .A(reg_file_1_a),
    .B(reg_file_1_b));
  Multiplexer #(.width(16)) multiplexer_1 (
    .in0(bit_extender_1_out), .in1(bit_extender_2_out), .out(multiplexer_1_out), .sel(MUX_IMM));
  Multiplexer #(.width(16)) multiplexer_2 (.in0(ram_1_dout), .in1(alu_main_1_s), .out(pc_main_1_p1), .sel(MEM_TO_REG));
  Multiplexer #(.width(16)) multiplexer_3 (
    .in0(reg_file_1_b), .in1(multiplexer_1_out), .out(multiplexer_3_out), .sel(LOAD_IMM));
  ALU_Main alu_main_1 (
    .A(reg_file_1_a), .B(multiplexer_3_out), .ALU_Control(ALU_OP), .S(alu_main_1_s));  // open: N, C, Z, V
  RAM #(.addrWidth(16), .dataWidth(16)) ram_1 (
    .addr(alu_main_1_s), .we(MEM_WRITE), .oe(MEM_READ), .clk(clock_3_out), .din(reg_file_1_b),
    .dout(ram_1_dout));
  Clock clock_3 (.out(clock_3_out));

  // Notes on the sheet:
  //   MEM_READ
  //   MEM_WRITE
  //   PC_ADRESS
  //   MUX_2
  //   MUX_3
  //   ALU_B0
  //   ALU_B1
  //   ALU_B2
  //   ALU_B3
  //   REG_WRITE_ENABLE
  //   MUX_1 - SELECT_IMM
  //   M2
endmodule
